# Fritzing sketch Programmer (saved by Fritzing 0.9.5d)
circuit board: 8.46667cm x 5.64444cm
perfboards: 1

parts:
  U1 = Voltage Regulator - Variable [package="TO220 [THT]"]
  Part1 = Arduino Mega 2560 (Rev3)
  R1 = Resistor [tolerance=±5% resistance=220 package=THT]
  R2 = Trimmer Potentiometer [maximum_resistance=1kΩ package=THT]
  IC2 = IC, DIP package, 4 pins [chip_label=StepUp]
  Q13 = PNP-Transistor [package="TO92 [THT]"]
  Q14 = NPN-Transistor [package="TO92 [THT]"]
  R3 = Resistor [tolerance=±5% resistance=1k package=THT]
  Q15 = PNP-Transistor [package="TO92 [THT]"]
  R4 = Resistor [tolerance=±5% resistance=1k package=THT]
  R5 = Resistor [tolerance=±5% resistance=1k package=THT]
  R6 = Resistor [tolerance=±5% resistance=1k package=THT]
  R7 = Resistor [tolerance=±5% resistance=1k package=THT]
  IC1 = IC, DIP package, 28 pins [chip_label=27C512]
  Q16 = NPN-Transistor [package="TO92 [THT]"]

nets:
  N1: U1.ADJ, R1.Pin_0, R2.leg2
  6V: U1.OUT, R1.Pin_1, Q15.E, IC1.pin28
  13V: U1.IN, IC2.pin3, Q13.E
  GND: Part1.GND, R2.wiper, IC2.pin1, IC2.pin4, R5.Pin_0, R6.Pin_0, R7.Pin_0, IC1.pin14
  5V: Part1.5V, IC2.pin2
  VppHigh: Part1.D3_PWM, R3.Pin_0
  GVppLow: Part1.D5_PWM, R4.Pin_1
  N2: Part1.D24, IC1.pin15
  N3: Part1.D26, IC1.pin16
  N4: Part1.D27, IC1.pin13
  N5: Part1.D28, IC1.pin17
  N6: Part1.D29, IC1.pin12
  N7: Part1.D30, IC1.pin18
  N8: Part1.D31, IC1.pin11
  N9: Part1.D32, IC1.pin19
  N10: Part1.D33, IC1.pin10
  N11: Part1.D34, IC1.pin20
  N12: Part1.D35, IC1.pin9
  N13: Part1.D36, IC1.pin21
  N14: Part1.D37, IC1.pin8
  N15: Part1.D39, IC1.pin7
  N16: Part1.D40, IC1.pin23
  N17: Part1.D41, IC1.pin6
  N18: Part1.D42, IC1.pin24
  N19: Part1.D43, IC1.pin5
  N20: Part1.D44, IC1.pin25
  N21: Part1.D45, IC1.pin4
  N22: Part1.D46, IC1.pin26
  N23: Part1.D47, IC1.pin3
  N24: Part1.D48, IC1.pin27
  N25: Part1.D49, IC1.pin2
  N26: Part1.D51, IC1.pin1
  N27: Q13.B, Q14.C
  GVpp: Q13.C, Q15.C, R5.Pin_1, IC1.pin22
  N28: Q14.E, R6.Pin_1
  N29: Q14.B, R3.Pin_1
  N30: Q15.B, Q16.C
  N31: R4.Pin_0, Q16.B
  N32: R7.Pin_1, Q16.E

// code stored in the sketch: eprom.ino
//FIXME
const int programPin=3;
const int readPin=4;
const int enablePin=2;

const unsigned long romSize=512*1024;

/*                  
 *Regular eprom pinout, uncommnet this one and comment the above                   
 *to burn regular eproms for use with other systems.
 *You may have to actually edit this for use with your console/8bit computer
 *The pinout from the eprom is different from the snes pinout
 */
int adrPins[20]={22,//eprom A0  snes A0
                  23,//eprom A1  snes A1
                  24,//eprom A2  snes A2
                  25,//eprom A3  snes A3
                  26,//eprom A4  snes A4
                  27,//eprom A5  snes A5
                  28,//eprom A6  snes A6
                  29,//eprom A7  snes A7
                  30,//eprom A8  snes A8
                  31,//eprom A9  snes A9
                  32,//eprom A10 snes A10
                  33,//eprom A11 snes A11
                  34,//eprom A12 snes A12
                  35,//eprom A13 snes A13
                  36,//eprom A14 snes A14
                  37,//eprom A15 snes A15
                  38,//eprom A16 snes A18 *
                  39,//eprom A17 snes A19 *
                  40,//eprom A18 snes A16 *
                  41 //eprom A19 snes A17 *
                  };

char dataPins[8]={5,6,7,8,9,10,11,12};

byte inByte=0;
unsigned int secH=0,secL=0;

void setup() {
  pinMode(programPin,OUTPUT);
  pinMode(readPin,OUTPUT);
  pinMode(enablePin,OUTPUT);
  for(int i=0;i<20;i++){
    pinMode(adrPins[i],OUTPUT);
  }
  digitalWrite(programPin,LOW);
  digitalWrite(readPin,LOW);
  digitalWrite(enablePin,HIGH);
  Serial.begin(250000);
  delay(1000);
  programMode();
}
int index=0;
void loop() {
  if(Serial.available()){
    inByte=Serial.read();
    if(inByte==0x55){
      while(Serial.available()==0);
      inByte=Serial.read();
      switch(inByte){
        case 'w':
          programMode();
          while(Serial.available()<2);
          secH=Serial.read();
          secL=Serial.read();
          writeSector(secH,secL);
          break;
        case 'r':
          readMode();
          readROM();
          break;
      }
    }
  }
}


//low level functions, direct ccontact with hardware pins
void programMode(){
  //data as output
  for(int i=0;i<8;i++){
    pinMode(dataPins[i],OUTPUT);
  }
  digitalWrite(readPin,LOW);
  digitalWrite(programPin,HIGH);
}
void readMode(){
  //data as input
  for(int i=0;i<8;i++){
    pinMode(dataPins[i],INPUT);
  }
  digitalWrite(programPin,LOW);
  digitalWrite(readPin,LOW);

}
void setAddress(uint32_t Addr){
    for(int i=0;i<8;i++){
      digitalWrite(adrPins[i],Addr&(1<<i));
    }
    Addr=Addr>>8;
    for(int i=0;i<8;i++){
      digitalWrite(adrPins[i+8],Addr&(1<<i));
    }
    Addr=Addr>>8;
    for(int i=0;i<4;i++){
      digitalWrite(adrPins[i+16],Addr&(1<<i));
    }
}
byte readByte(unsigned long adr){
    byte data;
    setAddress(adr);
    digitalWrite(enablePin,LOW);
    delayMicroseconds(1);
    for(int i=7;i>=0;i--){
        data=data<<1;
        data|=digitalRead(dataPins[i])&1;
    }
    digitalWrite(enablePin,HIGH);
    return data;
}
void setData(char Data){
  for(int i=0;i<8;i++){
      digitalWrite(dataPins[i],Data&(1<<i));
  }
}
void programByte(byte Data){
  setData(Data);
  //Vpp pulse
  delayMicroseconds(4);
  digitalWrite(enablePin,LOW);
  delayMicroseconds(60);
  digitalWrite(enablePin,HIGH);
}

void writeSector(unsigned char sectorH,unsigned char sectorL){
  byte dataBuffer[128];
  unsigned long address=0;
  byte CHK=sectorH,CHKreceived;
  CHK^=sectorL;

  address=sectorH;
  address=(address<<8)|sectorL;
  address*=128;

  for(int i=0;i<128;i++){
        while(Serial.available()==0);
        dataBuffer[i]=Serial.read();
        CHK ^= dataBuffer[i];
  }
  while(Serial.available()==0);
  CHKreceived=Serial.read();
  programMode();
  //only program the bytes if the checksum is equal to the one received
  if(CHKreceived==CHK){
    for (int i = 0; i < 128; i++){
      setAddress(address++);
      programByte(dataBuffer[i]);
    }
  Serial.write(CHK);
  }
  readMode();

}
int readROM(){
  unsigned long num=1024*1024;
  unsigned long address;
  byte data,checksum=0;
  address=0;
  //read mode
  readMode();
  //start frame
  digitalWrite(readPin,LOW);
  digitalWrite(programPin,LOW);
  for(long i;i<1048576;i++){//1048576
    data=readByte(address++);
    Serial.write(data);
    //checksum^=data;
  }
  digitalWrite(readPin,HIGH);

  //Serial.write(checksum);
  //Serial.write(0xAA);
}
